# Fritzing sketch main (saved by Fritzing 0.9.2b)
circuit board: 8.52876cm x 5.6388cm
breadboards: 1

parts:
  U1 = atmega328 [package=dip]
  XTAL1 = Crystal [frequency="16 Mhz" package=THT]
  IC1 = IC, DIP package, 20 pins [chip_label=74LVC244]
  Raspberry_Pi_2 = Raspberry Pi 2
  C4 = Ceramic Capacitor [capacitance=100nF package="100 mil [THT, multilayer]"]
  C3 = Ceramic Capacitor [capacitance=100nF package="100 mil [THT, multilayer]"]
  R1 = Resistor [tolerance=±5% resistance=10k package=THT]
  Q1 = MOSFET-NCHANNEL [package=to-92]
  R3 = Resistor [tolerance=±5% resistance=10k package=THT]
  R2 = Resistor [tolerance=±5% resistance=100k package=THT]
  C1 = Ceramic Capacitor [capacitance=22pF package="100 mil [THT, multilayer]"]
  C2 = Ceramic Capacitor [capacitance=22pF package="100 mil [THT, multilayer]"]
  R4 = Resistor [tolerance=±5% resistance=10k package=THT]
  R5 = Resistor [tolerance=±5% resistance=10k package=THT]
  R6 = Resistor [tolerance=±5% resistance=10k package=THT]
  R7 = Resistor [tolerance=±5% resistance=10k package=THT]
  Port3 = shrouded pin header, 6 pins [form="♂ (shrouded male)"]
  Port2 = shrouded pin header, 6 pins [form="♂ (shrouded male)"]
  Port1 = shrouded pin header, 6 pins [form="♂ (shrouded male)"]
  GPS = female pin header, 9 pins [form="♀ (female)"]
  M2 = male pin header, 2 pins [form="♂ (male)"]
  M3 = male pin header, 2 pins [form="♂ (male)"]
  M4 = male pin header, 2 pins [form="♂ (male)"]
  M1 = male pin header, 2 pins [form="♂ (male)"]
  A3 = male pin header, 3 pins [form="♂ (male)"]
  A2 = male pin header, 3 pins [form="♂ (male)"]
  A1 = male pin header, 3 pins [form="♂ (male)"]
  ISP = double row female pin header, 6 pins [form="♀ (female)"]
  A0 = male pin header, 3 pins [form="♂ (male)"]
  J1 = female pin header, 2 pins [form="♀ (female)"]
  J2 = female pin header, 2 pins [form="♀ (female)"]
  Disp = male pin header, 3 pins [form="♂ (male)"]
  Port4 = shrouded pin header, 6 pins [form="♂ (shrouded male)"]
  Q2 = MOSFET-NCHANNEL [package=to-92]
  Q3 = MOSFET-NCHANNEL [package=to-92]
  Q4 = MOSFET-NCHANNEL [package=to-92]  # not connected

nets:
  AVR_RST: U1.RESET, Q1.D, R3.Pin_1, ISP.pin3
  AVR_RX: U1.D0_(RX), J2.pin2
  AVR_TX: U1.D1_(TX), J1.pin2
  AVR_D2: U1.D2, M1.pin1
  PWM0: U1.D3_(PWM), M1.pin2
  AVR_D4: U1.D4, M2.pin1
  5V: U1.VCC, U1.AVCC, Raspberry_Pi_2.5V, C4.0, C3.1, R3.Pin_0, R6.Pin_1, R7.Pin_1, Port3.pin1, Port2.pin1, Port1.pin1, A3.pin2, A2.pin2, A1.pin2, ISP.pin6, A0.pin2, Disp.pin2, Port4.pin1
  GND: U1.GND, IC1.pin10, IC1.pin11, IC1.pin13, IC1.pin15, IC1.pin17, Raspberry_Pi_2.GND, C4.1, C3.0, Q1.S, R2.Pin_0, C1.1, C2.1, Port3.pin3, Port3.pin6, Port2.pin3, Port2.pin6, Port1.pin3, Port1.pin6, GPS.pin7, A3.pin3, A2.pin3, A1.pin3, ISP.pin4, A0.pin3, Disp.pin3, Port4.pin3, Port4.pin6
  N1: U1.XLAT1, XTAL1.pin_1, C2.0
  N2: U1.XLAT2, XTAL1.pin_0, C1.0
  PWM1: U1.D5_(PWM), M2.pin2
  PWM2: U1.D6_(PWM), M3.pin2
  AVR_D7: U1.D7, M3.pin1
  AVR_D8: U1.D8, M4.pin1
  PWM3: U1.D9_(PWM), M4.pin2
  N3: U1.D10_(PWM), Disp.pin1
  AVR_MOSI: U1.D11_(PWM), IC1.pin14, ISP.pin5
  AVR_MISO: U1.D12, IC1.pin8, ISP.pin1
  AVR_SCK: U1.D13, IC1.pin16, ISP.pin2
  ADC0: U1.A0, A0.pin1
  ADC1: U1.A1, A1.pin1
  ADC2: U1.A2, A2.pin1
  ADC3: U1.A3, A3.pin1
  5V_SDA: U1.A4, R7.Pin_0, Port3.pin4, Port2.pin4, Port1.pin4, Port4.pin4, Q2.D
  5V_SCL: U1.A5, R6.Pin_0, Port3.pin5, Port2.pin5, Port1.pin5, Port4.pin5, Q3.D
  PI_CE0: IC1.pin1, Raspberry_Pi_2.GPIO8, R1.Pin_0
  PI_SCK: IC1.pin4, Raspberry_Pi_2.GPIO11
  PI_MOSI: IC1.pin6, Raspberry_Pi_2.GPIO10
  PI_MISO: IC1.pin12, Raspberry_Pi_2.GPIO9
  N4: IC1.pin18, Q1.G, R2.Pin_1
  3.3V: IC1.pin19, IC1.pin20, R1.Pin_1, R4.Pin_1, R5.Pin_1, Port3.pin2, Port2.pin2, Port1.pin2, GPS.pin1, Port4.pin2, Q2.G, Q3.G
  3.3V_SDA: Raspberry_Pi_2.GPIO2, R4.Pin_0, Q2.S
  3.3V_SCL: Raspberry_Pi_2.GPIO3, R5.Pin_0, Q3.S
  N5: Raspberry_Pi_2.GPIO26, GPS.pin2
  N6: Raspberry_Pi_2.GPIO15, GPS.pin5, J2.pin1
  N7: Raspberry_Pi_2.GPIO14, GPS.pin6, J1.pin1

notes:
  3.3V
  VBAT
  FIX
  TX
  RX
  GND
  VIN
  PPS
  EN
  I2C Level Shifter
  Raspberry Pi Header
  Atmel ATMEGA 328p
  ATMEGA Programmer
  ADC Header
  Expansion Ports
  Motors
  5V
  G
  A
  Rx
  E
  Pathfinder v1.1
  ○
  Andy Condon ©2016
  M

custom parts:
  MOSFET-NCHANNEL: Generic NMOS footprint
