# Fritzing sketch navigator (saved by Fritzing 0.9.2b)
breadboards: 1

parts:
  U1 = atmega328 [package=dip]  # not connected
  Raspberry_Pi_2 = Raspberry Pi 2
  GPS1 = Adafruit Ultimate GPS Breakout

nets:
  N1: Raspberry_Pi_2.GPIO15, GPS1.TX
  N2: Raspberry_Pi_2.GPIO14, GPS1.RX
